# Fritzing sketch hallmoeba_breadboard_3k_keypad (saved by Fritzing 1.0.1rc)
breadboards: 1

parts:
  Mod1 = Raspberry Pi Pico
  S1 = Pushbutton [package="[THT]"]
  S2 = Pushbutton [package="[THT]"]
  S3 = Pushbutton [package="[THT]"]
  IC1 = DIP - 12 pins [chip_label=HALL package="DIP (Dual Inline) [THT]"]
  IC2 = DIP - 12 pins [chip_label=HALL package="DIP (Dual Inline) [THT]"]
  IC3 = DIP - 12 pins [chip_label=HALL package="DIP (Dual Inline) [THT]"]

nets:
  N1: Mod1.pin_3, Mod1.pin_8, Mod1.pin_13, Mod1.pin_18, Mod1.pin_23, Mod1.pin_28, Mod1.pin_33, Mod1.pin_38, S1.Pin_1, S1.Pin_2, S2.Pin_3, S2.Pin_4, S3.Pin_3, S3.Pin_4, IC1.pin4, IC2.pin4, IC3.pin4
  N2: Mod1.pin_22, S3.Pin_1, S3.Pin_2
  N3: Mod1.pin_24, S2.Pin_1, S2.Pin_2
  N4: Mod1.pin_25, S1.Pin_3, S1.Pin_4
  N5: Mod1.pin_31, IC1.pin2
  N6: Mod1.pin_32, IC2.pin2
  N7: Mod1.pin_34, IC3.pin2
  N8: Mod1.pin_35, Mod1.pin_36, IC1.pin6, IC2.pin6, IC3.pin6
  N9: Mod1.pin_39, Mod1.pin_40

custom parts:
  Raspberry Pi Pico: Raspberry Pi Pico. Based around the RP2040 microcontroller the Pico is a low cost microcontroller device bringing Raspberry Pi quality, cost, and easy of use to the microcontroller space. Jan 2021, Split part in to two versions: tht (this one) and SMD. This one will drill holes for a .1 in header in pcb to allow plugging in the module as well as providing pads to solder the module to the top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
  DIP - 12 pins: A DIP stand-in part for whatever IC you want. With 12 pins on a 300mil dual inline package (DIP) footprint.
